# Fritzing sketch ldr_led (saved by Fritzing 0.9.2b)
breadboards: 1

parts:
  Part1 = Arduino Uno (Rev3)
  R1 = Resistor [tolerance=±5% resistance=10 package=THT]
  LED1 = LED - 5mm [color="Red (633nm)" package="5 mm [THT]"]
  R2 = Resistor [tolerance=±5% resistance=220 package=THT]
  R3 = Photocell (LDR) [package=THT]

nets:
  N1: Part1.A0, R1.Pin_1, R3.pin_0
  N2: Part1.D9_PWM, LED1.cathode
  N3: Part1.5V, R3.pin_1
  N4: Part1.GND, R1.Pin_0, R2.Pin_0
  N5: LED1.anode, R2.Pin_1
