# Fritzing sketch push_led (saved by Fritzing 0.9.2b)
breadboards: 1

parts:
  Part1 = Arduino Uno (Rev3)
  S1 = Pushbutton [package="[THT]"]
  R1 = Resistor [tolerance=±5% resistance=10 package=THT]
  LED1 = LED - 5mm [color="Red (633nm)" package="5 mm [THT]"]

nets:
  N1: Part1.D13/SCK, LED1.anode
  N2: Part1.GND, R1.Pin_0, LED1.cathode
  N3: Part1.D7, Part1.5V, S1.Pin_1, S1.Pin_2, S1.Pin_3, S1.Pin_4, R1.Pin_1
